# Fritzing sketch maups (saved by Fritzing 0.8.7b)
circuit board: 6.88566cm x 5.36311cm

parts:
  MAUPS = Arduino Uno (Rev3)
  X_MOT = female pin header, 4 pins [form="♀ (female)"]
  MS_X = double row female pin header, 6 pins [form="♀ (female)"]
  Y_MOT = female pin header, 4 pins [form="♀ (female)"]
  MS_Y = double row female pin header, 6 pins [form="♀ (female)"]
  C2 = Electrolytic Capacitor [capacitance=100nF voltage=16V package="100 mil [THT, electrolytic]"]
  R1 = Resistor [tolerance=±5% resistance=10k package=THT]
  X_ENDSTOP = female pin header, 2 pins [form="♀ (female)"]
  Y_ENDSTOP = female pin header, 2 pins [form="♀ (female)"]
  U1 = Voltage Regulator [package=to220-adj]
  R2 = Resistor [tolerance=±5% resistance=10 package=THT]
  R3 = Resistor [tolerance=±5% resistance=10 package=THT]
  R4 = Resistor [tolerance=±5% resistance=10 package=THT]
  R5 = Resistor [tolerance=±5% resistance=10 package=THT]
  D1 = Rectifier Diode [part_number=1N4001 package="300 mil [THT]"]
  C3 = Electrolytic Capacitor [capacitance=10µF package="100 mil [THT, electrolytic]"]
  LASER = Screw terminal - 2 pins [package=THT]
  Q1 = MOSFET-NCHANNEL [package=to220v]
  R7 = Resistor [tolerance=±5% resistance=10 package=THT]
  R8 = Resistor [tolerance=±5% resistance=100k package=THT]
  Q2 = MOSFET-NCHANNEL [package=to220v]
  R9 = Resistor [tolerance=±5% resistance=10 package=THT]
  R10 = Resistor [tolerance=±5% resistance=100k package=THT]
  FAN = Screw terminal - 2 pins [package=THT]
  U2 = POT [package=3362u]
  Pololu_X = Pololu A4988 [package=SO16]
  C1 = Electrolytic Capacitor [capacitance=100nF voltage=16V package="100 mil [THT, electrolytic]"]
  Pololu_Y = Pololu A4988 [package=SO16]

nets:
  N1: MAUPS.A3, R9.Pin_1, R10.Pin_1
  N2: MAUPS.D8, R1.Pin_1, Pololu_X.ENABLE, Pololu_Y.ENABLE
  N3: MAUPS.D9_PWM, X_ENDSTOP.pin1
  N4: MAUPS.D10_PWM/SS, Y_ENDSTOP.pin1
  N5: MAUPS.D12/MISO, R7.Pin_1, R8.Pin_1
  GND: MAUPS.GND, C2.-, X_ENDSTOP.pin2, Y_ENDSTOP.pin2, Q1.S, R8.Pin_0, Q2.S, R10.Pin_0, Pololu_X.GND, C1.-, Pololu_Y.GND
  N6: MAUPS.D2, Pololu_X.STEP
  N7: MAUPS.D3_PWM, Pololu_Y.STEP
  N8: MAUPS.D5_PWM, Pololu_X.DIR
  N9: MAUPS.D6_PWM, Pololu_Y.DIR
  VDD: MAUPS.5V, MS_X.pin1, MS_X.pin2, MS_X.pin3, MS_Y.pin1, MS_Y.pin2, MS_Y.pin3, R1.Pin_0, Pololu_X.VDD, Pololu_Y.VDD
  N10: MAUPS.VIN, C2.+, U1.IN, FAN.pin2, Pololu_X.VMOT, C1.+, Pololu_Y.VMOT
  N11: X_MOT.pin1, Pololu_X.2B
  N12: X_MOT.pin2, Pololu_X.2A
  N13: X_MOT.pin3, Pololu_X.1A
  N14: X_MOT.pin4, Pololu_X.1B
  N15: MS_X.pin4, Pololu_X.MS1
  N16: MS_X.pin5, Pololu_X.MS2
  N17: MS_X.pin6, Pololu_X.MS3
  N18: Y_MOT.pin1, Pololu_Y.2B
  N19: Y_MOT.pin2, Pololu_Y.2A
  N20: Y_MOT.pin3, Pololu_Y.1A
  N21: Y_MOT.pin4, Pololu_Y.1B
  N22: MS_Y.pin4, Pololu_Y.MS1
  N23: MS_Y.pin5, Pololu_Y.MS2
  N24: MS_Y.pin6, Pololu_Y.MS3
  N25: U1.ADJ, U2.E
  N26: U1.OUT, R2.Pin_0, R3.Pin_0, R4.Pin_0, R5.Pin_0, D1.anode, C3.+, LASER.pin2
  N27: R2.Pin_1, R3.Pin_1, R4.Pin_1, R5.Pin_1, U2.S
  N28: D1.cathode, C3.-, LASER.pin1, Q1.D
  N29: Q1.G, R7.Pin_0
  N30: Q2.G, R9.Pin_0
  N31: Q2.D, FAN.pin1
  N32: Pololu_X.RESET, Pololu_X.SLEEP
  N33: Pololu_Y.RESET, Pololu_Y.SLEEP

custom parts:
  Pololu A4988: The A4988 stepper motor driver carrier is a breakout board for Allegro’s A4988 microstepping bipolar stepper motor driver. The driver features adjustable current limiting, overcurrent and overtemperature protection, and five different microstep resolutions (down to 1/16-step). It operates from 8 – 35 V and can deliver up to approximately 1 A per phase without a heat sink or forced air flow (it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
